# Fritzing sketch OttoPi-01 (saved by Fritzing 0.9.3b)
circuit board: 8.46667cm x 5.64444cm
perfboards: 1

parts:
  MCU1 = Raspberry Pi Zero
  J16 = female pin header, 5 pins [form="♀ (female)"]
  J17 = female pin header, 5 pins [form="♀ (female)"]
  LED1 = LED - 5mm [color="Red (633nm)" package="5 mm [THT]"]  # not connected
  S1 = Pushbutton [package="[THT]"]
  R1 = Resistor [tolerance=±5% resistance=220 package=THT]  # not connected
  S2 = Toggle Switch [package=THT]
  J18 = female pin header, 2 pins [form="♀ (female)"]
  J19 = female pin header, 2 pins [form="♀ (female)"]
  J20 = female pin header, 2 pins [form="♀ (female)"]
  J3 = female pin header, 4 pins [form="♀ (female)"]
  J4 = female pin header, 4 pins [form="♀ (female)"]
  J5 = female pin header, 4 pins [form="♀ (female)"]
  J6 = female pin header, 4 pins [form="♀ (female)"]
  J7 = female pin header, 4 pins [form="♀ (female)"]
  J8 = female pin header, 4 pins [form="♀ (female)"]
  J9 = female pin header, 4 pins [form="♀ (female)"]
  J15 = female pin header, 4 pins [form="♀ (female)"]

nets:
  N1: MCU1.pin_1, MCU1.pin_17, J16.pin1, J17.pin1
  N2: MCU1.pin_2, MCU1.pin_4, J19.pin1
  N3: MCU1.pin_3, J16.pin2, J17.pin2
  N4: MCU1.pin_5, J16.pin3, J17.pin3
  N5: MCU1.pin_6, MCU1.pin_9, MCU1.pin_14, MCU1.pin_20, MCU1.pin_34, J16.pin5, J17.pin5, J18.pin2, J19.pin2, J20.pin2, J3.pin2, J4.pin2, J5.pin2, J6.pin2, J7.pin2, J8.pin2, J9.pin2, J15.pin2
  N6: MCU1.pin_7, J16.pin4, J17.pin4
  N7: S1.Pin_1, S1.Pin_2
  N8: S1.Pin_3, S1.Pin_4
  N9: S2.L1, J20.pin1
  N10: S2.COM, J18.pin1, J3.pin1, J4.pin1, J5.pin1, J6.pin1, J7.pin1, J8.pin1, J9.pin1, J15.pin1
  N11: J3.pin3, J3.pin4
  N12: J4.pin3, J4.pin4
  N13: J5.pin3, J5.pin4
  N14: J6.pin3, J6.pin4
  N15: J7.pin3, J7.pin4
  N16: J8.pin3, J8.pin4
  N17: J9.pin3, J9.pin4
  N18: J15.pin3, J15.pin4
