# Fritzing sketch OttoPi-04 (saved by Fritzing 0.9.3b)
circuit board: 6.54415cm x 7.02234cm
perfboards: 2

parts:
  J1 = female pin header, 3 pins [form="♀ (female)"]
  R1 = Resistor [tolerance=±5% resistance=220 package=THT]
  SPK = female pin header, 2 pins [form="♀ (female)"]
  J3 = female pin header, 3 pins [form="♀ (female)"]
  R2 = Resistor [tolerance=±5% resistance=10k package=THT]
  SW2 = Toggle Switch [package=THT]
  S1 = Pushbutton [package="[THT]"]
  J24 = female pin header, 5 pins [form="♀ (female)"]
  VCC1 = Battery
  J2 = female pin header, 3 pins [form="♀ (female)"]
  J27 = female pin header, 4 pins [form="♀ (female)"]
  LED1 = LED - 5mm [color="Red (633nm)" package="5 mm [THT]"]
  J30 = female pin header, 1 pin [form="♀ (female)"]
  J28 = female pin header, 1 pin [form="♀ (female)"]
  J16 = female pin header, 5 pins [form="♀ (female)"]
  J7 = female pin header, 3 pins [form="♀ (female)"]
  J5 = female pin header, 3 pins [form="♀ (female)"]
  J6 = female pin header, 3 pins [form="♀ (female)"]
  J4 = female pin header, 3 pins [form="♀ (female)"]
  J35 = female pin header, 1 pin [form="♀ (female)"]
  SW1 = female pin header, 2 pins [form="♀ (female)"]
  J32 = female pin header, 3 pins [form="♀ (female)"]
  J33 = female pin header, 1 pin [form="♀ (female)"]
  MCU1 = Raspberry Pi Zero
  J32_2 = female pin header, 2 pins [form="♀ (female)"]
  R3 = Resistor [tolerance=±5% resistance=150 package=THT]
  C1 = Ceramic Capacitor [capacitance=100nF voltage=50V package="200 mil [THT, multilayer]"]
  J8 = female pin header, 3 pins [form="♀ (female)"]
  J9 = female pin header, 3 pins [form="♀ (female)"]
  GND = female pin header, 2 pins [form="♀ (female)"]

nets:
  N1: J1.pin1, J3.pin1, S1.Pin_1, S1.Pin_2, J24.pin1, VCC1.-, J2.pin1, LED1.cathode, J28.pin1, J16.pin1, J7.pin1, J5.pin1, J6.pin1, J4.pin1, SW1.pin1, J32.pin2, J33.pin1, MCU1.pin_6, MCU1.pin_9, MCU1.pin_14, MCU1.pin_20, MCU1.pin_25, MCU1.pin_30, MCU1.pin_34, MCU1.pin_39, J32_2.pin1, C1.1, J8.pin1, J9.pin1, GND.pin1
  N2: J1.pin2, J3.pin2, SW2.COM, J2.pin2, J30.pin1, J7.pin2, J5.pin2, J6.pin2, J4.pin2, J32_2.pin2, J8.pin2, J9.pin2
  N3: R1.Pin_0, LED1.anode
  N4: R1.Pin_1, MCU1.pin_38
  N5: SPK.pin1, J27.pin3
  N6: SPK.pin2, J27.pin4
  N7: R2.Pin_0, S1.Pin_3, S1.Pin_4, SW1.pin2, MCU1.pin_40
  N8: R2.Pin_1, MCU1.pin_37
  N9: SW2.L1, VCC1.+, GND.pin2
  N10: J24.pin2, J16.pin2, MCU1.pin_7
  N11: J24.pin3, J16.pin3, MCU1.pin_5
  N12: J24.pin4, J16.pin4, MCU1.pin_3
  N13: J24.pin5, J16.pin5, MCU1.pin_1, MCU1.pin_17
  N14: J35.pin1, MCU1.pin_2, MCU1.pin_4
  N15: J32.pin1, R3.Pin_1, C1.0
  N16: MCU1.pin_33, R3.Pin_0
