# Fritzing sketch OttoPi-05a (saved by Fritzing 0.9.3b)
circuit board: 6.7507cm x 8.08932cm
perfboards: 1

parts:
  VCC1 = Battery
  MCU1 = Raspberry Pi Zero
  J1 = female pin header, 3 pins [form="♀ (female)"]
  S1 = Toggle Switch [package=THT]

nets:
  N1: VCC1.-, J1.pin2
  N2: VCC1.+, S1.COM
  N3: MCU1.pin_1, MCU1.pin_17
  N4: MCU1.pin_2, MCU1.pin_4, J1.pin1
  N5: MCU1.pin_6, MCU1.pin_9, MCU1.pin_14, MCU1.pin_20, MCU1.pin_25, MCU1.pin_30, MCU1.pin_34, MCU1.pin_39
  N6: J1.pin3, S1.L1
